// Logisim project s-mips.circ as structural Verilog: 20 circuits, main circuit S-MIPS Board
module S_MIPS_Board (
  input  DESHABILITAR_DISPATCHER,
  output halt
);

  wire button_1_out, CLK, CS, d_ff_1_q, LCLR, LoadRAM, LoadRAMOn, LW, R_R_W, R_W, ram_dispatcher_1_finished,
       RCS, Reset_out, RST, TTY_EN;
  wire [2:0] KDB;
  wire [3:0] LMask, Mask, ram_1_read_time, ram_1_write_time, RMask;
  wire [6:0] KDB_DATA, TTY_DATA;
  wire [15:0] Addr, LAddr, RAddr;
  wire [31:0] I0, I1, I2, I3, LData, ram_1_data_out_0, ram_1_data_out_1, ram_1_data_out_2, ram_1_data_out_3,
       RI0, RI1, RI2, RI3;

  TTY #(.rows(25), .cols(80)) tty_1 (.data(TTY_DATA), .clk(CLK), .we(TTY_EN), .clr(RST));
  not not_1 (LoadRAMOn, ram_dispatcher_1_finished);
  RAM_Dispatcher ram_dispatcher_1 (
    .WriteTime(ram_1_write_time), .Clock(CLK), .Data(LData), .Address(LAddr), .Mask(LMask),
    .Finished(ram_dispatcher_1_finished), .Write(LW), .CLR(LCLR));
  Keyboard #(.buflen(64)) keyboard_1 (.clk(CLK), .re(KDB[0]), .avail(KDB[2]), .data(KDB_DATA));  // open: clr
  RAM ram_1 (
    .Address(RAddr), .Data_Out_0(ram_1_data_out_0), .Data_Out_1(ram_1_data_out_1),
    .Data_Out_2(ram_1_data_out_2), .Data_Out_3(ram_1_data_out_3), .Data_In_0(RI0), .Data_In_1(RI1),
    .Data_In_2(RI2), .Data_In_3(RI3), .Mask(RMask), .nRead_Write(R_R_W), .Chip_Select(RCS),
    .Read_Time(ram_1_read_time), .Reset(button_1_out), .Write_Time(ram_1_write_time));
  Button button_1 (.out(button_1_out));
  D_Flip_Flop d_ff_1 (.clk(CLK), .D(1'b1), .Q(d_ff_1_q), .reset(Reset_out));  // open: Qn, preset, en
  Button Reset (.out(Reset_out));
  S_MIPS s_mips_1 (
    .Kbd_Enable(KDB[0]), .Address(Addr), .Kbd_Clear(KDB[1]), .Kbd_Available(KDB[2]), .RAM_In_0(I0),
    .Kbd_ASCII_Data(KDB_DATA), .RAM_In_1(I1), .TTY_Enable(TTY_EN), .RAM_In_2(I2), .RAM_In_3(I3),
    .TTY_ASCII_Data(TTY_DATA), .Reset(RST), .RAM_Out_0(ram_1_data_out_0), .Clock(CLK),
    .RAM_Out_1(ram_1_data_out_1), .Stop(halt), .RAM_Out_2(ram_1_data_out_2), .RAM_Out_3(ram_1_data_out_3),
    .Mask(Mask), .Read_Time(ram_1_read_time), .Write_Time(ram_1_write_time), .nRead_Write(R_W),
    .Chip_Select(CS));
  D_Flip_Flop d_ff_2 (.clk(CLK), .D(d_ff_1_q), .Qn(LCLR), .reset(Reset_out));  // open: Q, preset, en
  or or_1 (RST, LCLR, LoadRAM);
  Clock clock_1 (.out(CLK));
  Multiplexer #(.width(32), .enable("false")) multiplexer_1 (.in0(I0), .in1(LData), .out(RI0), .sel(LoadRAM));
  Multiplexer #(.width(32), .enable("false")) multiplexer_2 (.in0(I1), .in1(LData), .out(RI1), .sel(LoadRAM));
  Multiplexer #(.width(32), .enable("false")) multiplexer_3 (.in0(I2), .in1(LData), .out(RI2), .sel(LoadRAM));
  Multiplexer #(.width(32), .enable("false")) multiplexer_4 (.in0(I3), .in1(LData), .out(RI3), .sel(LoadRAM));
  and and_1 (LoadRAM, ~DESHABILITAR_DISPATCHER, LoadRAMOn);  // AND_Gate
  Multiplexer #(.width(16), .enable("false")) multiplexer_5 (.in0(Addr), .in1(LAddr), .out(RAddr), .sel(LoadRAM));
  Multiplexer #(.width(4), .enable("false")) multiplexer_6 (.in0(Mask), .in1(LMask), .out(RMask), .sel(LoadRAM));
  Multiplexer #(.enable("false")) multiplexer_7 (.in0(CS), .in1(LW), .out(RCS), .sel(LoadRAM));
  Multiplexer #(.enable("false")) multiplexer_8 (.in0(R_W), .in1(LW), .out(R_R_W), .sel(LoadRAM));

  // Notes on the sheet:
  //   NO MODIFICAR
  //   Keyboard
endmodule

module S_MIPS (
  input  Kbd_Available,
  input  [6:0] Kbd_ASCII_Data,
  input  [31:0] RAM_Out_0,
  input  [31:0] RAM_Out_1,
  input  Reset,
  input  [31:0] RAM_Out_2,
  input  Clock,
  input  [31:0] RAM_Out_3,
  input  [3:0] Read_Time,
  input  [3:0] Write_Time,
  output Kbd_Enable,
  output [15:0] Address,
  output Kbd_Clear,
  output TTY_Enable,
  output [6:0] TTY_ASCII_Data,
  output Stop,
  output [31:0] RAM_In_0,
  output [31:0] RAM_In_1,
  output [31:0] RAM_In_2,
  output [31:0] RAM_In_3,
  output [3:0] Mask,
  output nRead_Write,
  output Chip_Select
);

  wire data_path_1_tty, HALT, HIT, LOAD_INST, or_1_out, PC, PC_ADDRESS, RAM_INST, RAM_READ, WRITE_RAM;
  wire [31:0] cache_1_b0, cache_1_b1, cache_1_b2, cache_1_b3, lb_1_output, MEMORY, RAM_DATA;

  or or_1 (or_1_out, RAM_READ, LOAD_INST);
  Cache cache_1 (
    .I0(RAM_Out_0), .I2(RAM_Out_2), .I1(RAM_Out_1), .I3(RAM_Out_3), .ADDR(Address), .RAM_READ(or_1_out),
    .CLK(Clock), .CLR(Reset), .WRITE(nRead_Write), .B0(cache_1_b0), .B1(cache_1_b1), .B2(cache_1_b2),
    .B3(cache_1_b3), .Hit(HIT), .LOAD_INSTRUCTION(LOAD_INST));
  Data_Path data_path_1 (
    .CLK(Clock), .RESET(Reset), .EN_PC(PC), .KEYBOARD(Kbd_ASCII_Data), .RAM_READ(RAM_READ),
    .LOAD_INST(LOAD_INST), .WRITE_RAM(WRITE_RAM), .MEMORY_INST(RAM_INST), .HALT(HALT),
    .MEMORY({MEMORY[31:20], Address, MEMORY[3:0]}), .RAM_DATA(RAM_DATA), .TTY(data_path_1_tty),
    .KBD(Kbd_Enable), .TTY_DATA(TTY_ASCII_Data), .PC_ADDRESS(PC_ADDRESS), .BANK0(cache_1_b0),
    .BANK1(cache_1_b1), .BANK2(cache_1_b2), .BANK3(cache_1_b3),
    .MEMORYI({MEMORY[31:20], Address, MEMORY[3:0]}));
  Control_Unit control_unit_1 (
    .CS(Chip_Select), .CLK(Clock), .RESET(Reset), .R_TIME(Read_Time), .W_TIME(Write_Time),
    .PC_ADDRESS(PC_ADDRESS), .WRITE(WRITE_RAM), .HALT(HALT), .RAM_INST(RAM_INST), .WRITE_2(nRead_Write),
    .PC(PC), .LOAD_INST(LOAD_INST), .RAM_READ(RAM_READ), .STOP(Stop), .HIT(HIT));
  Demultiplexer #(.select(2), .width(32), .enable("false")) demultiplexer_1 (
    .out0(RAM_In_0), .out1(RAM_In_1), .out2(RAM_In_2), .out3(RAM_In_3), .in(lb_1_output), .sel(MEMORY[3:2]));
  LB lb_1 (.INSTRUCTION(RAM_DATA), .OUTPUT(lb_1_output));
  Demultiplexer #(.select(2), .enable("false")) demultiplexer_2 (
    .out0(Mask[0]), .out1(Mask[1]), .out2(Mask[2]), .out3(Mask[3]), .in(1'b1), .sel(MEMORY[3:2]));
  and and_1 (TTY_Enable, data_path_1_tty, PC);

  assign Kbd_Clear = Reset;

  // Other names for the same wires on the sheet: CLK = Clock; CS = Chip_Select; KBD_AVAIL = Kbd_Available;
  //   CLR = Reset; KBD_CLR = Reset; KBD_DATA[6:0] = Kbd_ASCII_Data; SELECTOR[1:0] = MEMORY[3:2];
  //   MEMORY[19:4] = Address; RAM_A[15:0] = Address; RAM_INPUT_0[31:0] = RAM_In_0; RAM_INPUT_1[31:0] = RAM_In_1;
  //   RAM_INPUT_2[31:0] = RAM_In_2; RAM_INPUT_3[31:0] = RAM_In_3; RAM_MASK[3:0] = Mask;
  //   RAM_OUTPUT_0[31:0] = RAM_Out_0; RAM_OUTPUT_1[31:0] = RAM_Out_1; RAM_OUTPUT_2[31:0] = RAM_Out_2;
  //   RAM_OUTPUT_3[31:0] = RAM_Out_3; RW = nRead_Write; TTY_DATA[6:0] = TTY_ASCII_Data

  // Notes on the sheet:
  //   RAM ADDRESS
  //   DATA FROM RAM
  //   DATA TO RAM
  //   DATA WRITE MASK
  //   RAM TIMING
  //   RAM CONTROL
  //   KEYBOARD
  //   TTY
  //   SEQUENCING
endmodule

module RAM (
  input  [15:0] Address,
  input  [31:0] Data_In_0,
  input  [31:0] Data_In_1,
  input  [31:0] Data_In_2,
  input  [31:0] Data_In_3,
  input  [3:0] Mask,
  input  nRead_Write,
  input  Chip_Select,
  input  Reset,
  output [31:0] Data_Out_0,
  output [31:0] Data_Out_1,
  output [31:0] Data_Out_2,
  output [31:0] Data_Out_3,
  output [3:0] Read_Time,
  output [3:0] Write_Time
);

  wire and_2_out, and_3_out, and_4_out, and_5_out, and_6_out, and_7_out, and_8_out, and_9_out, Changed, CLK,
       comparator_2_eq, comparator_3_eq, comparator_4_eq, comparator_5_eq, comparator_6_eq, Count,
       demultiplexer_3_out0, Idle, Idle_q, Load, Load0, Load1, nand_1_out, or_1_out, or_2_out, or_3_out,
       or_4_out, or_5_out, or_6_out, or_7_out, or_8_out, or_9_out, or_10_out, Proc_q, Update_Mem, Zero_Time;
  wire [3:0] counter_1_q, multiplexer_1_out, subtractor_1_out;
  wire [31:0] register_1_q, register_2_q, register_3_q, register_4_q, register_5_q;

  // Probe on 4'b0011
  // Probe on 4'b0010
  Multiplexer #(.width(4), .enable("false")) multiplexer_1 (
    .in0(4'b0011), .in1(4'b0010), .out(multiplexer_1_out), .sel(nRead_Write));
  or or_1 (or_1_out, Idle, Update_Mem);
  or or_2 (or_2_out, ~Chip_Select, Reset);  // OR_Gate
  Subtractor #(.width(4)) subtractor_1 (.a(multiplexer_1_out), .b(4'b0010), .out(subtractor_1_out));  // open: bin, bout
  D_Flip_Flop u_Idle (.clk(CLK), .D(or_1_out), .Q(Idle_q), .preset(or_2_out));  // open: Qn, en, reset
  Demultiplexer #(.enable("false")) demultiplexer_1 (.out0(Idle), .out1(Load0), .in(Idle_q), .sel(Changed));
  // Probe on counter_1_q
  Counter #(.width(4), .max('hf)) counter_1 (
    .load(Load), .D(subtractor_1_out), .count(Count), .Q(counter_1_q), .clk(CLK), .clr(or_3_out));  // open: carry
  or or_3 (or_3_out, ~Chip_Select, Reset);  // OR_Gate
  Comparator #(.width(4), .mode("unsigned")) comparator_1 (
    .a(4'b0000), .b(counter_1_q), .eq(Zero_Time));  // open: gt, lt
  or or_4 (or_4_out, Count, Load0, Load1);
  Register #(.width(32)) register_1 (.D(Data_In_0), .en(Chip_Select), .Q(register_1_q), .clk(CLK), .clr(or_5_out));
  or or_5 (or_5_out, ~Chip_Select, Reset);  // OR_Gate
  Register #(.width(32)) register_2 (.D(Data_In_1), .en(Chip_Select), .Q(register_2_q), .clk(CLK), .clr(or_6_out));
  or or_6 (or_6_out, ~Chip_Select, Reset);  // OR_Gate
  Register #(.width(32)) register_3 (.D(Data_In_2), .en(Chip_Select), .Q(register_3_q), .clk(CLK), .clr(or_7_out));
  or or_7 (or_7_out, ~Chip_Select, Reset);  // OR_Gate
  Register #(.width(32)) register_4 (.D(Data_In_3), .en(Chip_Select), .Q(register_4_q), .clk(CLK), .clr(or_8_out));
  or or_8 (or_8_out, ~Chip_Select, Reset);  // OR_Gate
  Register #(.width(32)) register_5 (
    .D({{11{1'b1}}, nRead_Write, Mask, Address}), .en(Chip_Select), .Q(register_5_q), .clk(CLK),
    .clr(or_9_out));
  or or_9 (or_9_out, ~Chip_Select, Reset);  // OR_Gate
  D_Flip_Flop Proc (.clk(CLK), .D(or_4_out), .Q(Proc_q), .reset(or_10_out));  // open: Qn, preset, en
  or or_10 (or_10_out, ~Chip_Select, Reset);  // OR_Gate
  Demultiplexer #(.enable("false")) demultiplexer_2 (
    .out0(Count), .out1(Update_Mem), .in(demultiplexer_3_out0), .sel(Zero_Time));
  Demultiplexer #(.enable("false")) demultiplexer_3 (
    .out0(demultiplexer_3_out0), .out1(Load1), .in(Proc_q), .sel(Changed));
  Clock clock_1 (.out(CLK));
  Comparator #(.width(32)) comparator_2 (.a(register_1_q), .b(Data_In_0), .eq(comparator_2_eq));  // open: gt, lt
  Comparator #(.width(32)) comparator_3 (.a(register_2_q), .b(Data_In_1), .eq(comparator_3_eq));  // open: gt, lt
  Comparator #(.width(32)) comparator_4 (.a(register_3_q), .b(Data_In_2), .eq(comparator_4_eq));  // open: gt, lt
  Comparator #(.width(32)) comparator_5 (.a(register_4_q), .b(Data_In_3), .eq(comparator_5_eq));  // open: gt, lt
  Comparator #(.width(32)) comparator_6 (
    .a(register_5_q), .b({{11{1'b1}}, nRead_Write, Mask, Address}), .eq(comparator_6_eq));  // open: gt, lt
  nand nand_1 (nand_1_out, comparator_6_eq, comparator_2_eq, comparator_3_eq, comparator_4_eq, comparator_5_eq);
  and and_1 (Changed, nand_1_out, Chip_Select);
  or or_11 (Load, Count, Load1, Load0);
  and and_2 (and_2_out, Mask[0], Update_Mem, nRead_Write);
  and and_3 (and_3_out, Mask[1], Update_Mem, nRead_Write);
  and and_4 (and_4_out, Mask[2], Update_Mem, nRead_Write);
  and and_5 (and_5_out, Mask[3], Update_Mem, nRead_Write);
  RAM_part #(.addrWidth(16), .dataWidth(32), .bus("separate")) ram_1 (
    .addr(Address), .din(Data_In_0), .data(Data_Out_0), .str(and_2_out), .sel(Chip_Select), .clk(CLK),
    .ld(and_6_out), .clr(Reset));
  and and_6 (and_6_out, ~nRead_Write, Idle);  // AND_Gate
  RAM_part #(.addrWidth(16), .dataWidth(32), .bus("separate")) ram_2 (
    .addr(Address), .din(Data_In_1), .data(Data_Out_1), .str(and_3_out), .sel(Chip_Select), .clk(CLK),
    .ld(and_7_out), .clr(Reset));
  and and_7 (and_7_out, ~nRead_Write, Idle);  // AND_Gate
  RAM_part #(.addrWidth(16), .dataWidth(32), .bus("separate")) ram_3 (
    .addr(Address), .din(Data_In_2), .data(Data_Out_2), .str(and_4_out), .sel(Chip_Select), .clk(CLK),
    .ld(and_8_out), .clr(Reset));
  and and_8 (and_8_out, ~nRead_Write, Idle);  // AND_Gate
  RAM_part #(.addrWidth(16), .dataWidth(32), .bus("separate")) ram_4 (
    .addr(Address), .din(Data_In_3), .data(Data_Out_3), .str(and_5_out), .sel(Chip_Select), .clk(CLK),
    .ld(and_9_out), .clr(Reset));
  and and_9 (and_9_out, ~nRead_Write, Idle);  // AND_Gate

  assign Read_Time = 4'b0011;
  assign Write_Time = 4'b0010;

  // Other names for the same wires on the sheet: M0 = Mask[0]; M1 = Mask[1]; M2 = Mask[2]; M3 = Mask[3];
  //   RW = nRead_Write; CLR = Reset; CS = Chip_Select; Load2 = Count

  // Notes on the sheet:
  //   NO MODIFICAR
  //   excepto quizás los valores RT y WT
  //   BANK0
  //   BANK1
  //   BANK2
  //   BANK3
endmodule

module RAM_Dispatcher (
  input  [3:0] WriteTime,
  input  Clock,
  input  CLR,
  output [31:0] Data,
  output [15:0] Address,
  output [3:0] Mask,
  output Finished,
  output Write
);

  wire demultiplexer_2_out1, demultiplexer_3_out1, End, IDLE_q, IncAddr, Load, or_1_out, or_2_out, While_q,
       WriteEnd;
  wire [3:0] counter_1_q;
  wire [31:0] CurrentAddress_q;

  Counter #(.width(32), .max('hffffffff)) CurrentAddress (
    .count(IncAddr), .Q({CurrentAddress_q[31:18], Address, CurrentAddress_q[1:0]}), .clk(Clock), .clr(CLR));  // open: load, D, carry
  or or_1 (or_1_out, IncAddr, demultiplexer_3_out1, Finished);
  D_Flip_Flop IDLE (.clk(Clock), .D(or_1_out), .Q(IDLE_q), .preset(CLR));  // open: Qn, en, reset
  Demultiplexer #(.enable("false")) demultiplexer_1 (.out0(Load), .out1(Finished), .in(IDLE_q), .sel(End));
  D_Flip_Flop While (.clk(Clock), .D(or_2_out), .Q(While_q), .reset(CLR));  // open: Qn, preset, en
  or or_2 (or_2_out, Write, Load);
  RAM_part #(.addrWidth(18), .dataWidth(32)) ram_1 (
    .addr({Address, CurrentAddress_q[1:0]}), .data(Data), .clk(Clock));  // open: sel, ld, clr
  Demultiplexer #(.enable("false")) demultiplexer_2 (
    .out0(Write), .out1(demultiplexer_2_out1), .in(While_q), .sel(WriteEnd));
  Decoder #(.select(2)) decoder_1 (
    .out0(Mask[0]), .out1(Mask[1]), .out2(Mask[2]), .out3(Mask[3]), .sel(CurrentAddress_q[1:0]));  // open: en
  Demultiplexer #(.enable("false")) demultiplexer_3 (
    .out0(IncAddr), .out1(demultiplexer_3_out1), .in(demultiplexer_2_out1), .sel(End));
  Counter #(.width(4), .max('hf)) counter_1 (
    .load(Load), .D(WriteTime), .count(Write), .Q(counter_1_q), .clk(Clock));  // open: carry, clr
  Comparator #(.width(32)) comparator_1 (.a(Data), .b({32{1'b1}}), .eq(End));  // open: gt, lt
  Comparator #(.width(4)) comparator_2 (.a(4'b0000), .b(counter_1_q), .eq(WriteEnd));  // open: gt, lt

  // Other names for the same wires on the sheet: CLK = Clock; Count = Write; WT[3:0] = WriteTime
endmodule

module Data_Path (
  input  [31:0] BANK0,
  input  [31:0] BANK1,
  input  [31:0] MEMORYI,
  input  [31:0] BANK2,
  input  [31:0] BANK3,
  input  CLK,
  input  RESET,
  input  EN_PC,
  input  [6:0] KEYBOARD,
  input  PC_ADDRESS,
  input  RAM_READ,
  input  LOAD_INST,
  output [31:0] MEMORY,
  output MEMORY_INST,
  output WRITE_RAM,
  output [6:0] TTY_DATA,
  output KBD,
  output [31:0] RAM_DATA,
  output TTY,
  output HALT
);

  wire and_1_out, and_2_out, BEQ, BGTZ, BLEZ, BLTZ, BNE, CSign, div, isUnsigned, J, JR, LW, M_or_D, MFHI,
       MFLO, NF, NOP, or_3_out, or_6_out, or_7_out, or_8_out, POP, PUSH, RF_WRITE, RND, SW, TYPE_I,
       Write_operation, ZF;
  wire [2:0] ALU_OP, SRF;
  wire [4:0] multiplexer_5_out, RD, RS, RT;
  wire [15:0] CONSTANT;
  wire [25:0] DESTINO_SALTO;
  wire [31:0] ALU_OUTPUT, bit_extender_1_out, bit_extender_2_out, branch_control_1_bc_out, DESTINY, HIGH,
       INSTRUCTION, LOW, multiplexer_1_out, multiplexer_2_out, multiplexer_4_out, PC, random_1_out,
       register_1_q, RT_t, SP;
  wire [31:7] RS_t;

  Multiplexer #(.select(2), .width(32), .enable("false")) multiplexer_1 (
    .in0(BANK0), .in1(BANK1), .in2(BANK2), .in3(BANK3), .out(multiplexer_1_out), .sel(MEMORYI[3:2]));
  assign bit_extender_1_out = {{16{CONSTANT[15]}}, CONSTANT};  // Bit_Extender bit_extender_1
  Multiplexer #(.width(32), .enable("false")) multiplexer_2 (
    .in0(bit_extender_1_out), .in1(bit_extender_2_out), .out(multiplexer_2_out), .sel(CSign));
  assign bit_extender_2_out = {{16{1'b0}}, CONSTANT};  // Bit_Extender bit_extender_2
  or or_1 (WRITE_RAM, SW, PUSH);
  Multiplexer #(.width(32), .enable("false")) multiplexer_3 (
    .in0({RS_t, TTY_DATA}), .in1(RT_t), .out(RAM_DATA), .sel(SW));
  LB lb_1 (.INSTRUCTION(multiplexer_1_out), .OUTPUT(INSTRUCTION));
  Multiplexer #(.width(32), .enable("false")) multiplexer_4 (
    .in0(RT_t), .in1(multiplexer_2_out), .out(multiplexer_4_out), .sel(TYPE_I));
  or or_2 (MEMORY_INST, LW, WRITE_RAM, POP);
  Register #(.width(32)) register_1 (.D(INSTRUCTION), .en(LOAD_INST), .Q(register_1_q), .clk(CLK), .clr(RESET));
  Instruction_Decoder instruction_decoder_1 (
    .Instruction(register_1_q), .Jr(JR), .Mfhi(MFHI), .Mflo(MFLO), .Pop(POP), .Push(PUSH), .Halt(HALT),
    .Tti(TTY), .Rnd(RND), .Kbd(KBD), .Lw(LW), .Sw(SW), .Beq(BEQ), .Bne(BNE), .Blez(BLEZ), .Bgtz(BGTZ),
    .Bltz(BLTZ), .J(J), .isUnsigned(isUnsigned), .AluOpCode(ALU_OP), .Inmediate(TYPE_I), .Rd(RD), .Rt(RT),
    .Rs(RS), .Constante(CONSTANT), .DestinoSalto(DESTINO_SALTO), .Mult_Div(M_or_D), .Nop(NOP),
    .Write_instruction(Write_operation), .odiv(div), .Sign_Const(CSign));  // open: RType, X
  ALU alu_1 (
    .ALU_Selector(ALU_OP), .X({RS_t, TTY_DATA}), .CLK(CLK), .Y(multiplexer_4_out), .HIGH(HIGH),
    .ALU_OUTPUT(ALU_OUTPUT), .LOW(LOW), .ZF(ZF), .NF(NF), .isUnsigned(isUnsigned), .div(div), .m_d(M_or_D));
  Memory_Address memory_address_1 (
    .ALU(ALU_OUTPUT), .PC(PC), .SP(SP), .POP(POP), .PUSH(PUSH), .LW(LW), .SW(SW), .PC_ADDRESS(PC_ADDRESS),
    .MEMORY(MEMORY));
  Branch_Control branch_control_1 (
    .BEQ(BEQ), .BNE(BNE), .BLEZ(BLEZ), .BGTZ(BGTZ), .BLTZ(BLTZ), .JR(JR), .J(J), .DEST(DESTINO_SALTO),
    .RS({RS_t, TTY_DATA}), .RT(RT_t), .PC(PC), .CONST(CONSTANT), .BC_OUT(branch_control_1_bc_out));
  Program_Counter program_counter_1 (
    .ENABLE(EN_PC), .PC_OUTPUT(PC), .RESET(RESET), .INPUT(branch_control_1_bc_out), .CLK(CLK));
  Multiplexer #(.width(5), .enable("false")) multiplexer_5 (.in0(RD), .in1(RT), .out(multiplexer_5_out), .sel(TYPE_I));
  or or_3 (or_3_out, LW, POP);
  Random #(.width(32)) random_1 (.clk(CLK), .next(RND), .out(random_1_out));  // open: clr
  and and_1 (and_1_out, EN_PC, Write_operation);
  or or_4 (RF_WRITE, and_1_out, and_2_out);
  and and_2 (and_2_out, or_3_out, RAM_READ);
  Multiplexer #(.select(3), .width(32), .enable("false")) multiplexer_6 (
    .in0(ALU_OUTPUT), .in1(LOW), .in2(HIGH), .in3(INSTRUCTION), .in4({{25{1'b0}}, KEYBOARD}),
    .in5(random_1_out), .out(DESTINY), .sel(SRF));  // open: in6, in7
  Register_File register_file_1 (
    .RESET(RESET), .PUSH(PUSH), .CLK(CLK), .POP(POP), .INPUT(DESTINY), .WRITE(RF_WRITE), .SelOutA(RS),
    .SELECTOR(multiplexer_5_out), .SelOutB(RT), .OutA({RS_t, TTY_DATA}), .Out31(SP), .OutB(RT_t),
    .EN_PC(EN_PC));
  or or_5 (SRF[2], KBD, RND);
  or or_6 (or_6_out, MFHI, POP);
  or or_7 (or_7_out, RND, MFLO);
  or or_8 (or_8_out, POP, LW);
  // Probe on SRF
  or or_9 (SRF[1], or_6_out, LW);
  or or_10 (SRF[0], or_7_out, or_8_out);

  // Other names for the same wires on the sheet: KBDINPUT[6:0] = KEYBOARD; RS_t[6:0] = TTY_DATA

  // Notes on the sheet:
  //   OUTPUTS
endmodule

module Control_Unit (
  input  CLK,
  input  RESET,
  input  [3:0] R_TIME,
  input  [3:0] W_TIME,
  input  WRITE,
  input  HALT,
  input  RAM_INST,
  input  HIT,
  output CS,
  output PC_ADDRESS,
  output WRITE_2,
  output PC,
  output LOAD_INST,
  output RAM_READ,
  output STOP
);

  wire CHIP1, CHIP2, d_ff_2_q, demultiplexer_1_out1, demultiplexer_2_out0, demultiplexer_3_out0,
       demultiplexer_4_out0, demultiplexer_5_out0, IDLE_q, or_2_out, or_3_out, or_4_out, or_5_out, or_6_out,
       or_8_out, RAM_RESET, ram_write_off, Read_of_ram, STOP_t, time_1_out, time_2_out;
  wire [3:0] multiplexer_1_out;

  or or_1 (PC, demultiplexer_4_out0, ram_write_off);
  or or_2 (or_2_out, demultiplexer_4_out0, ram_write_off, demultiplexer_1_out1);
  D_Flip_Flop d_ff_1 (.clk(CLK), .D(or_3_out), .Q(CHIP1), .reset(RESET));  // open: Qn, preset, en
  or or_3 (or_3_out, demultiplexer_2_out0, Read_of_ram);
  Demultiplexer #(.enable("false")) demultiplexer_1 (
    .out0(Read_of_ram), .out1(demultiplexer_1_out1), .in(IDLE_q), .sel(RESET));
  D_Flip_Flop IDLE (.clk(CLK), .D(or_2_out), .Q(IDLE_q), .preset(RESET));  // open: Qn, en, reset
  Demultiplexer #(.enable("false")) demultiplexer_2 (
    .out0(demultiplexer_2_out0), .out1(LOAD_INST), .in(CHIP1), .sel(or_4_out));
  or or_4 (or_4_out, time_1_out, HIT);
  Time time_1 (.START(1'b1), .OUT(time_1_out), .TIME(R_TIME), .CLK(CLK), .RESET(Read_of_ram));
  or or_5 (or_5_out, STOP, STOP_t);
  D_Flip_Flop u_HALT (.clk(CLK), .D(or_5_out), .Q(STOP), .reset(RESET));  // open: Qn, preset, en
  D_Flip_Flop d_ff_2 (.clk(CLK), .D(LOAD_INST), .Q(d_ff_2_q), .reset(RESET));  // open: Qn, preset, en
  Demultiplexer #(.enable("false")) demultiplexer_3 (
    .out0(demultiplexer_3_out0), .out1(STOP_t), .in(d_ff_2_q), .sel(HALT));
  or or_6 (or_6_out, demultiplexer_5_out0, RAM_RESET);
  Multiplexer #(.width(4), .enable("false")) multiplexer_1 (
    .in0(R_TIME), .in1(W_TIME), .out(multiplexer_1_out), .sel(WRITE));
  Demultiplexer #(.enable("false")) demultiplexer_4 (
    .out0(demultiplexer_4_out0), .out1(RAM_RESET), .in(demultiplexer_3_out0), .sel(RAM_INST));
  D_Flip_Flop d_ff_3 (.clk(CLK), .D(or_6_out), .Q(CHIP2), .reset(RESET));  // open: Qn, preset, en
  or or_7 (PC_ADDRESS, CHIP1, Read_of_ram, PC);
  Demultiplexer #(.enable("false")) demultiplexer_5 (
    .out0(demultiplexer_5_out0), .out1(RAM_READ), .in(CHIP2), .sel(or_8_out));
  or or_8 (or_8_out, time_2_out, HIT);
  Time time_2 (.START(1'b1), .OUT(time_2_out), .TIME(multiplexer_1_out), .CLK(CLK), .RESET(RAM_RESET));
  D_Flip_Flop d_ff_4 (.clk(CLK), .D(RAM_READ), .Q(ram_write_off), .reset(RESET));  // open: Qn, preset, en
  or or_9 (CS, CHIP1, CHIP2);
  and and_1 (WRITE_2, CHIP2, WRITE);

  // Other names for the same wires on the sheet: ram_write = RAM_RESET; Read_of_ram_off = LOAD_INST;
  //   TIMER_RESET = Read_of_ram
endmodule

module ALU (
  input  [2:0] ALU_Selector,
  input  CLK,
  input  [31:0] X,
  input  [31:0] Y,
  input  isUnsigned,
  input  div,
  input  m_d,
  output [31:0] ALU_OUTPUT,
  output [31:0] HIGH,
  output ZF,
  output NF,
  output [31:0] LOW
);

  wire [31:0] ADD, AND, div_1_output, div_1_r, mult_1_hi, mult_1_lo, multiplexer_2_out, multiplexer_3_out,
       NOR, OR, SLT, SUB, XOR;

  assign AND = X & Y;  // AND_Gate and_1, 32 bits wide
  assign OR = X | Y;  // OR_Gate or_1, 32 bits wide
  assign NOR = ~(X | Y);  // NOR_Gate nor_1, 32 bits wide
  assign XOR = X ^ Y;  // XOR_Gate xor_1, 32 bits wide
  X_Y x_y_1 (.X(X), .Y(Y), .is_X_Y(SLT), .isUnsigned(isUnsigned));
  Adder #(.width(32)) adder_1 (.a(X), .b(Y), .out(ADD));  // open: cin, cout
  Subtractor #(.width(32)) subtractor_1 (.a(X), .b(Y), .out(SUB));  // open: bin, bout
  Mult mult_1 (.X(X), .Y(Y), .Lo(mult_1_lo), .Hi(mult_1_hi), .IsUnsigned(isUnsigned));
  Div div_1 (.X(X), .isUnsigned(isUnsigned), .Y(Y), .\output (div_1_output), .R(div_1_r));
  Multiplexer #(.select(3), .width(32), .enable("false")) multiplexer_1 (
    .in0(ADD), .in1(SUB), .in2(SLT), .in3(AND), .in4(OR), .in5(NOR), .in6(XOR), .out(ALU_OUTPUT),
    .sel(ALU_Selector));  // open: in7
  Multiplexer #(.width(32), .enable("false")) multiplexer_2 (
    .in0(mult_1_hi), .in1(div_1_r), .out(multiplexer_2_out), .sel(div));
  Multiplexer #(.width(32), .enable("false")) multiplexer_3 (
    .in0(mult_1_lo), .in1(div_1_output), .out(multiplexer_3_out), .sel(div));
  Comparator #(.width(32)) comparator_1 (.a(ALU_OUTPUT), .b({32{1'b0}}), .eq(ZF), .lt(NF));  // open: gt
  Register #(.width(32)) register_1 (.D(multiplexer_2_out), .en(m_d), .Q(HIGH), .clk(CLK));  // open: clr
  Register #(.width(32)) register_2 (.D(multiplexer_3_out), .en(m_d), .Q(LOW), .clk(CLK));  // open: clr

  // Notes on the sheet:
  //   ALU
endmodule

module Register_File (
  input  RESET,
  input  PUSH,
  input  CLK,
  input  POP,
  input  [31:0] INPUT,
  input  WRITE,
  input  [4:0] SelOutA,
  input  [4:0] SELECTOR,
  input  [4:0] SelOutB,
  input  EN_PC,
  output [31:0] OutA,
  output [31:0] OutB,
  output [31:0] Out31
);

  wire and_1_out, L0, L1, L2, L3, L4, L5, L6, L7, L8, L9, L10, L11, L12, L13, L14, L15, L16, L17, L18, L19,
       L20, L21, L22, L23, L24, L25, L26, L27, L28, L29, L30, L31, Lsp, or_1_out;
  wire [31:0] adder_1_out, multiplexer_1_out, multiplexer_2_out, R0, R1, R2, R3, R4, R5, R6, R7, R8, R9, R10,
       R11, R12, R13, R14, R15, R16, R17, R18, R19, R20, R21, R22, R23, R24, R25, R26, R27, R28, R29, R30,
       SP_IN, subtractor_1_out;

  Register #(.width(32)) register_1 (.D({32{1'b0}}), .en(L0), .Q(R0), .clk(CLK), .clr(RESET));
  Register #(.width(32)) register_2 (.D(INPUT), .en(L4), .Q(R4), .clk(CLK), .clr(RESET));
  Register #(.width(32)) register_3 (.D(INPUT), .en(L8), .Q(R8), .clk(CLK), .clr(RESET));
  Register #(.width(32)) register_4 (.D(INPUT), .en(L12), .Q(R12), .clk(CLK), .clr(RESET));
  Register #(.width(32)) register_5 (.D(INPUT), .en(L16), .Q(R16), .clk(CLK), .clr(RESET));
  Register #(.width(32)) register_6 (.D(INPUT), .en(L20), .Q(R20), .clk(CLK), .clr(RESET));
  Register #(.width(32)) register_7 (.D(INPUT), .en(L24), .Q(R24), .clk(CLK), .clr(RESET));
  Register #(.width(32)) register_8 (.D(INPUT), .en(L28), .Q(R28), .clk(CLK), .clr(RESET));
  or or_1 (or_1_out, PUSH, POP);
  or or_2 (Lsp, RESET, and_1_out, L31);
  and and_1 (and_1_out, or_1_out, EN_PC);
  Subtractor #(.width(32)) subtractor_1 (.a(Out31), .b(32'h4), .out(subtractor_1_out));  // open: bin, bout
  Multiplexer #(.width(32), .enable("false")) multiplexer_1 (
    .in0(subtractor_1_out), .in1(adder_1_out), .out(multiplexer_1_out), .sel(POP));
  Adder #(.width(32)) adder_1 (.a(32'h4), .b(Out31), .out(adder_1_out));  // open: cin, cout
  Register #(.width(32)) register_9 (.D(INPUT), .en(L1), .Q(R1), .clk(CLK), .clr(RESET));
  Register #(.width(32)) register_10 (.D(INPUT), .en(L5), .Q(R5), .clk(CLK), .clr(RESET));
  Register #(.width(32)) register_11 (.D(INPUT), .en(L9), .Q(R9), .clk(CLK), .clr(RESET));
  Register #(.width(32)) register_12 (.D(INPUT), .en(L13), .Q(R13), .clk(CLK), .clr(RESET));
  Register #(.width(32)) register_13 (.D(INPUT), .en(L17), .Q(R17), .clk(CLK), .clr(RESET));
  Register #(.width(32)) register_14 (.D(INPUT), .en(L21), .Q(R21), .clk(CLK), .clr(RESET));
  Register #(.width(32)) register_15 (.D(INPUT), .en(L25), .Q(R25), .clk(CLK), .clr(RESET));
  Register #(.width(32)) register_16 (.D(INPUT), .en(L29), .Q(R29), .clk(CLK), .clr(RESET));
  Multiplexer #(.width(32), .enable("false")) multiplexer_2 (
    .in0(multiplexer_1_out), .in1({32{1'b1}}), .out(multiplexer_2_out), .sel(RESET));
  Multiplexer #(.width(32), .enable("false")) multiplexer_3 (
    .in0(multiplexer_2_out), .in1(INPUT), .out(SP_IN), .sel(L31));
  Register #(.width(32)) register_17 (.D(INPUT), .en(L2), .Q(R2), .clk(CLK), .clr(RESET));
  Register #(.width(32)) register_18 (.D(INPUT), .en(L6), .Q(R6), .clk(CLK), .clr(RESET));
  Register #(.width(32)) register_19 (.D(INPUT), .en(L10), .Q(R10), .clk(CLK), .clr(RESET));
  Register #(.width(32)) register_20 (.D(INPUT), .en(L14), .Q(R14), .clk(CLK), .clr(RESET));
  Register #(.width(32)) register_21 (.D(INPUT), .en(L18), .Q(R18), .clk(CLK), .clr(RESET));
  Register #(.width(32)) register_22 (.D(INPUT), .en(L22), .Q(R22), .clk(CLK), .clr(RESET));
  Register #(.width(32)) register_23 (.D(INPUT), .en(L26), .Q(R26), .clk(CLK), .clr(RESET));
  Register #(.width(32)) register_24 (.D(INPUT), .en(L30), .Q(R30), .clk(CLK), .clr(RESET));
  Register #(.width(32)) register_25 (.D(INPUT), .en(L3), .Q(R3), .clk(CLK), .clr(RESET));
  Register #(.width(32)) register_26 (.D(INPUT), .en(L7), .Q(R7), .clk(CLK), .clr(RESET));
  Register #(.width(32)) register_27 (.D(INPUT), .en(L11), .Q(R11), .clk(CLK), .clr(RESET));
  Register #(.width(32)) register_28 (.D(INPUT), .en(L15), .Q(R15), .clk(CLK), .clr(RESET));
  Register #(.width(32)) register_29 (.D(INPUT), .en(L19), .Q(R19), .clk(CLK), .clr(RESET));
  Register #(.width(32)) register_30 (.D(INPUT), .en(L23), .Q(R23), .clk(CLK), .clr(RESET));
  Register #(.width(32)) register_31 (.D(INPUT), .en(L27), .Q(R27), .clk(CLK), .clr(RESET));
  Register #(.width(32)) register_32 (.D(SP_IN), .en(Lsp), .Q(Out31), .clk(CLK));  // open: clr
  Multiplexer #(.select(5), .width(32), .enable("false")) multiplexer_4 (
    .in0(R0), .in1(R1), .in2(R2), .in3(R3), .in4(R4), .in5(R5), .in6(R6), .in7(R7), .in8(R8), .in9(R9),
    .in10(R10), .in11(R11), .in12(R12), .in13(R13), .in14(R14), .in15(R15), .in16(R16), .in17(R17),
    .in18(R18), .in19(R19), .in20(R20), .in21(R21), .in22(R22), .in23(R23), .in24(R24), .in25(R25),
    .in26(R26), .in27(R27), .in28(R28), .in29(R29), .in30(R30), .in31(Out31), .out(OutA), .sel(SelOutA));
  Multiplexer #(.select(5), .width(32), .enable("false")) multiplexer_5 (
    .in0(R0), .in1(R1), .in2(R2), .in3(R3), .in4(R4), .in5(R5), .in6(R6), .in7(R7), .in8(R8), .in9(R9),
    .in10(R10), .in11(R11), .in12(R12), .in13(R13), .in14(R14), .in15(R15), .in16(R16), .in17(R17),
    .in18(R18), .in19(R19), .in20(R20), .in21(R21), .in22(R22), .in23(R23), .in24(R24), .in25(R25),
    .in26(R26), .in27(R27), .in28(R28), .in29(R29), .in30(R30), .in31(Out31), .out(OutB), .sel(SelOutB));
  Demultiplexer #(.select(5), .enable("false")) demultiplexer_1 (
    .out0(L0), .out1(L1), .out2(L2), .out3(L3), .out4(L4), .out5(L5), .out6(L6), .out7(L7), .out8(L8),
    .out9(L9), .out10(L10), .out11(L11), .out12(L12), .out13(L13), .out14(L14), .out15(L15), .out16(L16),
    .out17(L17), .out18(L18), .out19(L19), .out20(L20), .out21(L21), .out22(L22), .out23(L23), .out24(L24),
    .out25(L25), .out26(L26), .out27(L27), .out28(L28), .out29(L29), .out30(L30), .out31(L31), .in(WRITE),
    .sel(SELECTOR));

  // Other names for the same wires on the sheet: Destino[31:0] = INPUT; R31[31:0] = Out31

  // Notes on the sheet:
  //   constante 0
  //   REGISTER FILE
  //   REGISTROS
  //   SP
  //   Cargar de los registros
  //   Escribir en los Registros
endmodule

module Program_Counter (
  input  [31:0] INPUT,
  input  RESET,
  input  ENABLE,
  input  CLK,
  output [31:0] PC_OUTPUT
);

  Register #(.width(32)) register_1 (.D(INPUT), .en(ENABLE), .Q(PC_OUTPUT), .clk(CLK), .clr(RESET));
endmodule

module Branch_Control (
  input  BEQ,
  input  BNE,
  input  BLEZ,
  input  BGTZ,
  input  BLTZ,
  input  JR,
  input  J,
  input  [25:0] DEST,
  input  [15:0] CONST,
  input  [31:0] RS,
  input  [31:0] RT,
  input  [31:0] PC,
  output [31:0] BC_OUT
);

  wire comparator_1_eq, comparator_2_eq, comparator_2_gt, comparator_2_lt, or_1_out, or_2_out, or_3_out,
       or_4_out, or_5_out, Rs__0, Rs___0, Rs____0, Rs____Rt, Rs___Rt;
  wire [1:0] Condition;
  wire [13:0] bit_extender_1_out;
  wire [31:0] PC_4, Pc___4__offset_4;

  Adder #(.width(32)) adder_1 (.a(PC), .b(32'h4), .out(PC_4));  // open: cin, cout
  assign bit_extender_1_out = {{13{CONST[15]}}, CONST[15]};  // Bit_Extender bit_extender_1
  Comparator #(.width(32)) comparator_1 (.a(RS), .b(RT), .eq(comparator_1_eq));  // open: gt, lt
  Comparator #(.width(32)) comparator_2 (
    .a(RS), .b({32{1'b0}}), .gt(comparator_2_gt), .eq(comparator_2_eq), .lt(comparator_2_lt));
  and and_1 (Rs___0, BLTZ, comparator_2_lt);
  and and_2 (Rs___Rt, BNE, ~comparator_1_eq);  // AND_Gate
  and and_3 (Rs____Rt, BEQ, comparator_1_eq);
  and and_4 (Rs__0, BGTZ, comparator_2_gt);
  or or_1 (or_1_out, comparator_2_eq, comparator_2_lt);
  Multiplexer #(.select(2), .width(32), .enable("false")) multiplexer_1 (
    .in0(PC_4), .in1(Pc___4__offset_4), .in2({PC[31:28], DEST, 2'b00}), .in3(RS), .out(BC_OUT),
    .sel(Condition));
  Adder #(.width(32)) adder_2 (
    .a(PC_4), .b({bit_extender_1_out, CONST, 2'b00}), .out(Pc___4__offset_4));  // open: cin, cout
  and and_5 (Rs____0, or_1_out, BLEZ);
  or or_2 (or_2_out, Rs___Rt, Rs____Rt);
  or or_3 (or_3_out, Rs__0, Rs____0);
  or or_4 (or_4_out, or_2_out, or_3_out);
  or or_5 (or_5_out, or_4_out, Rs___0);
  or or_6 (Condition[1], JR, J);
  or or_7 (Condition[0], or_5_out, JR);
  // Probe on Condition

  // Other names for the same wires on the sheet: OFFSET[15:0] = CONST; jmp_to[31:2] = {PC[31:28], DEST}
endmodule

module Memory_Address (
  input  POP,
  input  PUSH,
  input  LW,
  input  SW,
  input  PC_ADDRESS,
  input  [31:0] SP,
  input  [31:0] PC,
  input  [31:0] ALU,
  output [31:0] MEMORY
);

  wire or_1_out, PP, STATE;
  wire [31:0] multiplexer_1_out, multiplexer_2_out, subtractor_1_out;

  or or_1 (or_1_out, SW, PP, LW);
  Multiplexer #(.width(32), .enable("false")) multiplexer_1 (.in0(ALU), .in1(SP), .out(multiplexer_1_out), .sel(PP));
  and and_1 (STATE, or_1_out, ~PC_ADDRESS);  // AND_Gate
  or or_2 (PP, PUSH, POP);
  Multiplexer #(.width(32), .enable("false")) multiplexer_2 (
    .in0(multiplexer_1_out), .in1(subtractor_1_out), .out(multiplexer_2_out), .sel(PUSH));
  Subtractor #(.width(32)) subtractor_1 (.a(SP), .b(32'h4), .out(subtractor_1_out));  // open: bin, bout
  Multiplexer #(.width(32), .enable("false")) multiplexer_3 (
    .in0(PC), .in1(multiplexer_2_out), .out(MEMORY), .sel(STATE));
endmodule

module Time (
  input  [3:0] TIME,
  input  START,
  input  CLK,
  input  RESET,
  output OUT
);

  wire [3:0] counter_1_q;

  Counter #(.width(4), .max('hf)) counter_1 (
    .count(START), .Q(counter_1_q), .clk(CLK), .clr(RESET));  // open: load, D, carry
  Comparator #(.width(4)) comparator_1 (.a(TIME), .b(counter_1_q), .eq(OUT));  // open: gt, lt
endmodule

module LB (
  input  [31:0] INSTRUCTION,
  output [31:0] OUTPUT
);


  assign OUTPUT = {INSTRUCTION[7:0], INSTRUCTION[15:8], INSTRUCTION[23:16], INSTRUCTION[31:24]};

  // Notes on the sheet:
  //   Little Endian to Big Endian
endmodule

module Instruction_Decoder (
  input  [31:0] Instruction,
  output Jr,
  output Mfhi,
  output Mflo,
  output Pop,
  output Push,
  output Halt,
  output Tti,
  output Rnd,
  output Kbd,
  output Lw,
  output Sw,
  output Beq,
  output Bne,
  output Blez,
  output Bgtz,
  output Bltz,
  output J,
  output Sign_Const,
  output isUnsigned,
  output [2:0] AluOpCode,
  output RType,
  output Inmediate,
  output [4:0] X,
  output [4:0] Rd,
  output [4:0] Rt,
  output [4:0] Rs,
  output [15:0] Constante,
  output [25:0] DestinoSalto,
  output Mult_Div,
  output odiv,
  output Nop,
  output Write_instruction
);

  wire Add, Addi, And, and_12_out, Andi, comparator_2_eq, comparator_3_eq, comparator_4_eq, comparator_5_eq,
       comparator_6_eq, comparator_7_eq, comparator_8_eq, comparator_9_eq, comparator_10_eq,
       comparator_11_eq, comparator_12_eq, comparator_13_eq, comparator_14_eq, comparator_15_eq,
       comparator_16_eq, comparator_17_eq, comparator_18_eq, comparator_19_eq, comparator_20_eq,
       comparator_21_eq, comparator_22_eq, comparator_23_eq, comparator_24_eq, Div, Divu, Mult, Mulu, Nor,
       OAdd, OAnd, OMult, OOr, Or, or_1_out, or_2_out, or_3_out, or_5_out, or_8_out, or_9_out, or_11_out,
       or_14_out, or_17_out, or_18_out, or_19_out, or_20_out, or_23_out, or_24_out, Ori, OSlt, OXor, Slt,
       Slti, Sltiu, Sltu, Sub, Xor, Xori;

  or or_1 (or_1_out, Lw, Sw);
  Comparator #(.width(6), .mode("unsigned")) comparator_1 (
    .a(Instruction[31:26]), .b({6{1'b0}}), .eq(RType));  // open: gt, lt
  and and_1 (Add, RType, comparator_2_eq);
  Comparator #(.width(6), .mode("unsigned")) comparator_2 (
    .a(Instruction[5:0]), .b(6'b100000), .eq(comparator_2_eq));  // open: gt, lt
  and and_2 (Sub, RType, comparator_3_eq);
  Comparator #(.width(6), .mode("unsigned")) comparator_3 (
    .a(Instruction[5:0]), .b(6'b100010), .eq(comparator_3_eq));  // open: gt, lt
  and and_3 (Mult, RType, comparator_4_eq);
  Comparator #(.width(6), .mode("unsigned")) comparator_4 (
    .a(Instruction[5:0]), .b(6'b011000), .eq(comparator_4_eq));  // open: gt, lt
  and and_4 (Mulu, RType, comparator_5_eq);
  Comparator #(.width(6), .mode("unsigned")) comparator_5 (
    .a(Instruction[5:0]), .b(6'b011001), .eq(comparator_5_eq));  // open: gt, lt
  and and_5 (Div, RType, comparator_6_eq);
  Comparator #(.width(6), .mode("unsigned")) comparator_6 (
    .a(Instruction[5:0]), .b(6'b011010), .eq(comparator_6_eq));  // open: gt, lt
  and and_6 (Divu, RType, comparator_7_eq);
  Comparator #(.width(6), .mode("unsigned")) comparator_7 (
    .a(Instruction[5:0]), .b(6'b011011), .eq(comparator_7_eq));  // open: gt, lt
  and and_7 (Slt, RType, comparator_8_eq);
  Comparator #(.width(6), .mode("unsigned")) comparator_8 (
    .a(Instruction[5:0]), .b(6'b101010), .eq(comparator_8_eq));  // open: gt, lt
  and and_8 (Sltu, RType, comparator_9_eq);
  Comparator #(.width(6), .mode("unsigned")) comparator_9 (
    .a(Instruction[5:0]), .b(6'b101011), .eq(comparator_9_eq));  // open: gt, lt
  and and_9 (Jr, RType, comparator_10_eq);
  Comparator #(.width(6), .mode("unsigned")) comparator_10 (
    .a(Instruction[5:0]), .b(6'b001000), .eq(comparator_10_eq));  // open: gt, lt
  and and_10 (Mfhi, RType, comparator_11_eq);
  Comparator #(.width(6), .mode("unsigned")) comparator_11 (
    .a(Instruction[5:0]), .b(6'b010000), .eq(comparator_11_eq));  // open: gt, lt
  and and_11 (Mflo, RType, comparator_12_eq);
  Comparator #(.width(6), .mode("unsigned")) comparator_12 (
    .a(Instruction[5:0]), .b(6'b010010), .eq(comparator_12_eq));  // open: gt, lt
  and and_12 (and_12_out, ~or_1_out, OAdd);  // AND_Gate
  or or_2 (or_2_out, and_12_out, OOr, Sub, OXor, Rnd);
  or or_3 (or_3_out, Kbd, And, Andi, Nor, Mfhi);
  Comparator #(.width(6), .mode("unsigned")) comparator_13 (
    .a(Instruction[5:0]), .b(6'b100100), .eq(comparator_13_eq));  // open: gt, lt
  Comparator #(.width(6), .mode("unsigned")) comparator_14 (
    .a(Instruction[5:0]), .b(6'b100101), .eq(comparator_14_eq));  // open: gt, lt
  Comparator #(.width(6), .mode("unsigned")) comparator_15 (
    .a(Instruction[5:0]), .b(6'b100111), .eq(comparator_15_eq));  // open: gt, lt
  Comparator #(.width(6), .mode("unsigned")) comparator_16 (
    .a(Instruction[5:0]), .b(6'b101000), .eq(comparator_16_eq));  // open: gt, lt
  Comparator #(.width(6), .mode("unsigned")) comparator_17 (
    .a(Instruction[31:26]), .b(6'b111000), .eq(comparator_17_eq));  // open: gt, lt
  Comparator #(.width(6), .mode("unsigned")) comparator_18 (
    .a(Instruction[5:0]), .b({6{1'b0}}), .eq(comparator_18_eq));  // open: gt, lt
  Comparator #(.width(6), .mode("unsigned")) comparator_19 (
    .a(Instruction[5:0]), .b(6'b000001), .eq(comparator_19_eq));  // open: gt, lt
  and and_13 (And, RType, comparator_13_eq);
  and and_14 (Or, RType, comparator_14_eq);
  and and_15 (Nor, RType, comparator_15_eq);
  and and_16 (Xor, RType, comparator_16_eq);
  and and_17 (Pop, comparator_17_eq, comparator_18_eq);
  and and_18 (Push, comparator_17_eq, comparator_19_eq);
  Comparator #(.width(6), .mode("unsigned")) comparator_20 (
    .a(Instruction[31:26]), .b({6{1'b1}}), .eq(comparator_20_eq));  // open: gt, lt
  and and_19 (Halt, comparator_20_eq, comparator_21_eq);
  Comparator #(.width(6), .mode("unsigned")) comparator_21 (
    .a(Instruction[5:0]), .b({6{1'b1}}), .eq(comparator_21_eq));  // open: gt, lt
  and and_20 (Tti, comparator_20_eq, comparator_22_eq);
  Comparator #(.width(6), .mode("unsigned")) comparator_22 (
    .a(Instruction[5:0]), .b(6'b000001), .eq(comparator_22_eq));  // open: gt, lt
  and and_21 (Rnd, comparator_20_eq, comparator_23_eq);
  Comparator #(.width(6), .mode("unsigned")) comparator_23 (
    .a(Instruction[5:0]), .b(6'b000010), .eq(comparator_23_eq));  // open: gt, lt
  and and_22 (Kbd, comparator_20_eq, comparator_24_eq);
  Comparator #(.width(6), .mode("unsigned")) comparator_24 (
    .a(Instruction[5:0]), .b(6'b000100), .eq(comparator_24_eq));  // open: gt, lt
  or or_4 (Write_instruction, or_2_out, or_3_out, Mflo, OSlt);
  Comparator #(.width(6), .mode("unsigned")) comparator_25 (
    .a(Instruction[31:26]), .b(6'b001000), .eq(Addi));  // open: gt, lt
  Comparator #(.width(6), .mode("unsigned")) comparator_26 (
    .a(Instruction[31:26]), .b(6'b001010), .eq(Slti));  // open: gt, lt
  Comparator #(.width(6), .mode("unsigned")) comparator_27 (
    .a(Instruction[31:26]), .b(6'b001011), .eq(Sltiu));  // open: gt, lt
  Comparator #(.width(6), .mode("unsigned")) comparator_28 (
    .a(Instruction[31:26]), .b(6'b001100), .eq(Andi));  // open: gt, lt
  Comparator #(.width(6), .mode("unsigned")) comparator_29 (
    .a(Instruction[31:26]), .b(6'b001101), .eq(Ori));  // open: gt, lt
  Comparator #(.width(6), .mode("unsigned")) comparator_30 (
    .a(Instruction[31:26]), .b(6'b001110), .eq(Xori));  // open: gt, lt
  // Probe on Instruction[5:0]
  Comparator #(.width(6), .mode("unsigned")) comparator_31 (
    .a(Instruction[31:26]), .b(6'b100011), .eq(Lw));  // open: gt, lt
  Comparator #(.width(6), .mode("unsigned")) comparator_32 (
    .a(Instruction[31:26]), .b(6'b101011), .eq(Sw));  // open: gt, lt
  Comparator #(.width(6), .mode("unsigned")) comparator_33 (
    .a(Instruction[31:26]), .b(6'b000100), .eq(Beq));  // open: gt, lt
  Comparator #(.width(6), .mode("unsigned")) comparator_34 (
    .a(Instruction[31:26]), .b(6'b000101), .eq(Bne));  // open: gt, lt
  Comparator #(.width(6), .mode("unsigned")) comparator_35 (
    .a(Instruction[31:26]), .b(6'b000110), .eq(Blez));  // open: gt, lt
  Comparator #(.width(6), .mode("unsigned")) comparator_36 (
    .a(Instruction[31:26]), .b(6'b000111), .eq(Bgtz));  // open: gt, lt
  Comparator #(.width(6), .mode("unsigned")) comparator_37 (
    .a(Instruction[31:26]), .b(6'b000001), .eq(Bltz));  // open: gt, lt
  or or_5 (or_5_out, OAnd, OOr);
  or or_6 (Sign_Const, or_5_out, OXor);
  coder coder_1 (
    .add(OAdd), .sub(Sub), .XlessthanY(OSlt), .\and (OAnd), .\or (OOr), .\nor (Nor), .\xor (OXor),
    .oo(AluOpCode[2]), .o1(AluOpCode[1]), .o2(AluOpCode[0]));
  // Probe on AluOpCode
  Comparator #(.width(6), .mode("unsigned")) comparator_38 (
    .a(Instruction[31:26]), .b(6'b000010), .eq(J));  // open: gt, lt
  or or_7 (OAdd, or_14_out, or_8_out);
  or or_8 (or_8_out, Add, Addi);
  or or_9 (or_9_out, Slt, Slti);
  or or_10 (OSlt, or_9_out, or_11_out);
  or or_11 (or_11_out, Sltu, Sltiu);
  or or_12 (isUnsigned, or_11_out, Mulu, Divu);
  or or_13 (OMult, Mult, Mulu);
  or or_14 (or_14_out, Lw, Sw);
  or or_15 (OOr, Or, Ori);
  or or_16 (OXor, Xor, Xori);
  or or_17 (or_17_out, Lw, Sw);
  or or_18 (or_18_out, Addi, Slti);
  or or_19 (or_19_out, Sltiu, Andi);
  or or_20 (or_20_out, Ori, Xori);
  or or_21 (OAnd, And, Andi);
  or or_22 (odiv, Div, Divu);
  or or_23 (or_23_out, or_17_out, or_18_out);
  or or_24 (or_24_out, or_19_out, or_20_out);
  or or_25 (Inmediate, or_24_out, or_23_out);
  or or_26 (Mult_Div, OMult, odiv);
  Comparator #(.width(32)) comparator_39 (.a(Instruction), .b({32{1'b0}}), .eq(Nop));  // open: gt, lt

  assign Constante = Instruction[15:0];
  assign DestinoSalto = Instruction[25:0];
  assign Rd = Instruction[15:11];
  assign Rs = Instruction[25:21];
  assign Rt = Instruction[20:16];
  assign X = Instruction[10:6];

  // Other names for the same wires on the sheet: FunCode[5:0] = Instruction[5:0]; OPCode[5:0] = Instruction[31:26];
  //   OpAluCode[2:0] = AluOpCode

  // Notes on the sheet:
  //   Tipo R
  //   Other R types
  //   Pila
  //   Identificar el funCode
  //   Insrucciones Especiales
  //   |
  //   |
  //   |
  //   Tipo I 
  //   pantalla para ir viendo los FunCode y su valor hexadecimal para las cts
  //   Funcion de Salida para la ALU
  //   |
  //   |
  //   |
  //   |
  //   |
  //   |
  //   |
  //   |
  //   |
  //   |
  //   |
  //   |
  //   |
  //   Tipo J
  //   Todos los outputs
endmodule

module X_Y (
  input  [31:0] X,
  input  [31:0] Y,
  input  isUnsigned,
  output [31:0] is_X_Y
);

  wire comparator_1_lt, comparator_2_lt;
  wire [31:0] multiplexer_1_out, multiplexer_2_out;

  Multiplexer #(.width(32), .enable("false")) multiplexer_1 (
    .in0({32{1'b0}}), .in1(32'h1), .out(multiplexer_1_out), .sel(comparator_1_lt));
  Comparator #(.width(32)) comparator_1 (.a(X), .b(Y), .lt(comparator_1_lt));  // open: gt, eq
  Comparator #(.width(32), .mode("unsigned")) comparator_2 (.a(X), .b(Y), .lt(comparator_2_lt));  // open: gt, eq
  Multiplexer #(.width(32), .enable("false")) multiplexer_2 (
    .in0({32{1'b0}}), .in1(32'h1), .out(multiplexer_2_out), .sel(comparator_2_lt));
  Multiplexer #(.width(32), .enable("false")) multiplexer_3 (
    .in0(multiplexer_1_out), .in1(multiplexer_2_out), .out(is_X_Y), .sel(isUnsigned));
endmodule

module Mult (
  input  [31:0] X,
  input  [31:0] Y,
  input  IsUnsigned,
  output [31:0] Lo,
  output [31:0] Hi
);

  wire [31:0] multiplexer_1_out, multiplexer_2_out, multiplexer_3_out, multiplier_1_cout, R31;

  Multiplexer #(.width(32), .enable("false")) multiplexer_1 (
    .in0({32{1'b0}}), .in1(Y), .out(multiplexer_1_out), .sel(X[31]));
  Multiplexer #(.width(32), .enable("false")) multiplexer_2 (
    .in0({32{1'b0}}), .in1(X), .out(multiplexer_2_out), .sel(Y[31]));
  Multiplexer #(.width(32), .enable("false")) multiplexer_3 (
    .in0({32{1'b0}}), .in1(R31), .out(multiplexer_3_out), .sel(IsUnsigned));
  Adder #(.width(32)) adder_1 (.a(multiplexer_1_out), .b(multiplexer_2_out), .out(R31));  // open: cin, cout
  Multiplier #(.width(32)) multiplier_1 (.a(X), .b(Y), .out(Lo), .cout(multiplier_1_cout));  // open: cin
  Adder #(.width(32)) adder_2 (.a(multiplier_1_cout), .b(multiplexer_3_out), .out(Hi));  // open: cin, cout
endmodule

module Div (
  input  [31:0] X,
  input  isUnsigned,
  input  [31:0] Y,
  output [31:0] \output ,
  output [31:0] R
);

  wire Sign, x31, Y31;
  wire [31:0] divider_1_out, divider_1_rem, negator_1_out, negator_2_out, xAbs, yAbs;

  and and_1 (x31, ~isUnsigned, X[31]);  // AND_Gate
  and and_2 (Y31, Y[31], ~isUnsigned);  // AND_Gate
  Negator #(.width(32)) negator_1 (.in(divider_1_out), .out(negator_1_out));
  Divider #(.width(32)) divider_1 (.a(xAbs), .b(yAbs), .out(divider_1_out), .rem(divider_1_rem));  // open: upper
  Negator #(.width(32)) negator_2 (.in(divider_1_rem), .out(negator_2_out));
  Multiplexer #(.width(32), .enable("false")) multiplexer_1 (
    .in0(divider_1_out), .in1(negator_1_out), .out(\output ), .sel(Sign));
  Multiplexer #(.width(32), .enable("false")) multiplexer_2 (
    .in0(divider_1_rem), .in1(negator_2_out), .out(R), .sel(Sign));
  _1 u_1_1 (.X(X), .Sign(x31), .minus_X(xAbs));
  xor xor_1 (Sign, x31, Y31);
  _1 u_1_2 (.X(Y), .Sign(Y31), .minus_X(yAbs));
endmodule

module _1 (
  input  [31:0] X,
  input  Sign,
  output [31:0] minus_X
);

  wire [31:0] negator_1_out;

  Negator #(.width(32)) negator_1 (.in(X), .out(negator_1_out));
  Multiplexer #(.width(32), .enable("false")) multiplexer_1 (.in0(X), .in1(negator_1_out), .out(minus_X), .sel(Sign));
endmodule

module coder (
  input  add,
  input  sub,
  input  XlessthanY,
  input  \and ,
  input  \or ,
  input  \nor ,
  input  \xor ,
  output oo,
  output o1,
  output o2
);

  wire and_1_out, and_2_out, and_3_out, and_4_out, and_5_out, and_6_out, not_1_out, not_2_out, not_3_out,
       not_4_out, not_5_out, not_6_out, not_7_out, not_8_out, not_9_out, not_10_out, not_11_out, not_12_out;

  not not_1 (not_1_out, add);
  not not_2 (not_2_out, sub);
  not not_3 (not_3_out, XlessthanY);
  not not_4 (not_4_out, \and );
  not not_5 (not_5_out, add);
  not not_6 (not_6_out, sub);
  not not_7 (not_7_out, \or );
  not not_8 (not_8_out, \nor );
  not not_9 (not_9_out, add);
  not not_10 (not_10_out, XlessthanY);
  not not_11 (not_11_out, \or );
  not not_12 (not_12_out, \xor );
  and and_1 (and_1_out, not_1_out, not_2_out);
  and and_2 (and_2_out, not_3_out, not_4_out);
  and and_3 (and_3_out, not_5_out, not_6_out);
  and and_4 (and_4_out, not_7_out, not_8_out);
  and and_5 (and_5_out, not_9_out, not_10_out);
  and and_6 (and_6_out, not_11_out, not_12_out);
  and and_7 (oo, and_1_out, and_2_out);
  and and_8 (o1, and_3_out, and_4_out);
  and and_9 (o2, and_5_out, and_6_out);
endmodule

module Cache (
  input  [31:0] I0,
  input  [31:0] I2,
  input  [31:0] I1,
  input  [31:0] I3,
  input  [15:0] ADDR,
  input  RAM_READ,
  input  CLK,
  input  CLR,
  input  WRITE,
  input  LOAD_INSTRUCTION,
  output Hit,
  output [31:0] B0,
  output [31:0] B1,
  output [31:0] B2,
  output [31:0] B3
);

  wire and_1_out, and_3_out, comparator_1_eq, L0, L1, L2, L3, L4, L5, L6, L7, not_1_out, V, Valid, valid0,
       valid1, valid2, valid3, valid4, valid5, valid6, valid7;
  wire [12:0] Tag0, Tag1, Tag2, Tag3, Tag4, Tag5, Tag6, Tag7, TagC;
  wire [31:0] multiplexer_3_out, multiplexer_5_out, multiplexer_7_out, multiplexer_9_out, R0, R1, R2, R3, R4,
       R5, R6, R7, R8, R9, R10, R11, R12, R13, R14, R15, R16, R17, R18, R19, R20, R21, R22, R23, R24, R25,
       R26, R27, R28, R29, R30, R31;

  Register #(.width(13)) register_1 (.D(ADDR[15:3]), .en(L0), .Q(Tag0), .clk(CLK));  // open: clr
  Register #(.width(13)) register_2 (.D(ADDR[15:3]), .en(L1), .Q(Tag1), .clk(CLK));  // open: clr
  Register #(.width(13)) register_3 (.D(ADDR[15:3]), .en(L2), .Q(Tag2), .clk(CLK));  // open: clr
  Register #(.width(13)) register_4 (.D(ADDR[15:3]), .en(L3), .Q(Tag3), .clk(CLK));  // open: clr
  Register #(.width(13)) register_5 (.D(ADDR[15:3]), .en(L4), .Q(Tag4), .clk(CLK));  // open: clr
  Register #(.width(13)) register_6 (.D(ADDR[15:3]), .en(L5), .Q(Tag5), .clk(CLK));  // open: clr
  Register #(.width(13)) register_7 (.D(ADDR[15:3]), .en(L6), .Q(Tag6), .clk(CLK));  // open: clr
  Register #(.width(13)) register_8 (.D(ADDR[15:3]), .en(L7), .Q(Tag7), .clk(CLK));  // open: clr
  Register #(.width(32)) register_9 (.D(I0), .en(L0), .Q(R0), .clk(CLK), .clr(CLR));
  Register #(.width(32)) register_10 (.D(I0), .en(L1), .Q(R4), .clk(CLK), .clr(CLR));
  Register #(.width(32)) register_11 (.D(I0), .en(L2), .Q(R8), .clk(CLK), .clr(CLR));
  Register #(.width(32)) register_12 (.D(I0), .en(L3), .Q(R12), .clk(CLK), .clr(CLR));
  Register #(.width(32)) register_13 (.D(I0), .en(L4), .Q(R16), .clk(CLK), .clr(CLR));
  Register #(.width(32)) register_14 (.D(I0), .en(L5), .Q(R20), .clk(CLK), .clr(CLR));
  Register #(.width(32)) register_15 (.D(I0), .en(L6), .Q(R24), .clk(CLK), .clr(CLR));
  Register #(.width(32)) register_16 (.D(I0), .en(L7), .Q(R28), .clk(CLK), .clr(CLR));
  and and_1 (and_1_out, ~Hit, RAM_READ);  // AND_Gate
  Register #(.width(32)) register_17 (.D(I1), .en(L0), .Q(R1), .clk(CLK), .clr(CLR));
  Register #(.width(32)) register_18 (.D(I1), .en(L1), .Q(R5), .clk(CLK), .clr(CLR));
  Register #(.width(32)) register_19 (.D(I1), .en(L2), .Q(R9), .clk(CLK), .clr(CLR));
  Register #(.width(32)) register_20 (.D(I1), .en(L3), .Q(R13), .clk(CLK), .clr(CLR));
  Register #(.width(32)) register_21 (.D(I1), .en(L4), .Q(R17), .clk(CLK), .clr(CLR));
  Register #(.width(32)) register_22 (.D(I1), .en(L5), .Q(R21), .clk(CLK), .clr(CLR));
  Register #(.width(32)) register_23 (.D(I1), .en(L6), .Q(R25), .clk(CLK), .clr(CLR));
  Register #(.width(32)) register_24 (.D(I1), .en(L7), .Q(R29), .clk(CLK), .clr(CLR));
  Multiplexer #(.select(3), .enable("false")) multiplexer_1 (
    .in0(valid0), .in1(valid1), .in2(valid2), .in3(valid3), .in4(valid4), .in5(valid5), .in6(valid6),
    .in7(valid7), .out(Valid), .sel(ADDR[2:0]));
  Multiplexer #(.select(3), .width(13), .enable("false")) multiplexer_2 (
    .in0(Tag0), .in1(Tag1), .in2(Tag2), .in3(Tag3), .in4(Tag4), .in5(Tag5), .in6(Tag6), .in7(Tag7),
    .out(TagC), .sel(ADDR[2:0]));
  Demultiplexer #(.select(3), .enable("false")) demultiplexer_1 (
    .out0(L0), .out1(L1), .out2(L2), .out3(L3), .out4(L4), .out5(L5), .out6(L6), .out7(L7), .in(and_1_out),
    .sel(ADDR[2:0]));
  Register #(.width(32)) register_25 (.D(I2), .en(L0), .Q(R2), .clk(CLK), .clr(CLR));
  Register #(.width(32)) register_26 (.D(I2), .en(L1), .Q(R6), .clk(CLK), .clr(CLR));
  Register #(.width(32)) register_27 (.D(I2), .en(L2), .Q(R10), .clk(CLK), .clr(CLR));
  Register #(.width(32)) register_28 (.D(I2), .en(L3), .Q(R14), .clk(CLK), .clr(CLR));
  Register #(.width(32)) register_29 (.D(I2), .en(L4), .Q(R18), .clk(CLK), .clr(CLR));
  Register #(.width(32)) register_30 (.D(I2), .en(L5), .Q(R22), .clk(CLK), .clr(CLR));
  Register #(.width(32)) register_31 (.D(I2), .en(L6), .Q(R26), .clk(CLK), .clr(CLR));
  Register #(.width(32)) register_32 (.D(I2), .en(L7), .Q(R30), .clk(CLK), .clr(CLR));
  Comparator #(.width(13)) comparator_1 (.a(TagC), .b(ADDR[15:3]), .eq(comparator_1_eq));  // open: gt, lt
  and and_2 (Hit, comparator_1_eq, and_3_out);
  and and_3 (and_3_out, Valid, ~WRITE);  // AND_Gate
  or or_1 (V, ~WRITE, LOAD_INSTRUCTION);  // OR_Gate
  Register #(.width(32)) register_33 (.D(I3), .en(L0), .Q(R3), .clk(CLK), .clr(CLR));
  Register #(.width(32)) register_34 (.D(I3), .en(L1), .Q(R7), .clk(CLK), .clr(CLR));
  Register #(.width(32)) register_35 (.D(I3), .en(L2), .Q(R11), .clk(CLK), .clr(CLR));
  Register #(.width(32)) register_36 (.D(I3), .en(L3), .Q(R15), .clk(CLK), .clr(CLR));
  Register #(.width(32)) register_37 (.D(I3), .en(L4), .Q(R19), .clk(CLK), .clr(CLR));
  Register #(.width(32)) register_38 (.D(I3), .en(L5), .Q(R23), .clk(CLK), .clr(CLR));
  Register #(.width(32)) register_39 (.D(I3), .en(L6), .Q(R27), .clk(CLK), .clr(CLR));
  Register #(.width(32)) register_40 (.D(I3), .en(L7), .Q(R31), .clk(CLK));  // open: clr
  D_Flip_Flop d_ff_1 (.clk(CLK), .D(V), .Q(valid0), .en(L0), .reset(CLR));  // open: Qn, preset
  D_Flip_Flop d_ff_2 (.clk(CLK), .D(V), .Q(valid1), .en(L1), .reset(CLR));  // open: Qn, preset
  D_Flip_Flop d_ff_3 (.clk(CLK), .D(V), .Q(valid2), .en(L2), .reset(CLR));  // open: Qn, preset
  D_Flip_Flop d_ff_4 (.clk(CLK), .D(V), .Q(valid3), .en(L3), .reset(CLR));  // open: Qn, preset
  D_Flip_Flop d_ff_5 (.clk(CLK), .D(V), .Q(valid4), .en(L4), .reset(CLR));  // open: Qn, preset
  D_Flip_Flop d_ff_6 (.clk(CLK), .D(V), .Q(valid5), .en(L5), .reset(CLR));  // open: Qn, preset
  D_Flip_Flop d_ff_7 (.clk(CLK), .D(V), .Q(valid6), .en(L6), .reset(CLR));  // open: Qn, preset
  D_Flip_Flop d_ff_8 (.clk(CLK), .D(V), .Q(valid7), .en(L7), .reset(CLR));  // open: Qn, preset
  Multiplexer #(.select(3), .width(32), .enable("false")) multiplexer_3 (
    .in0(R0), .in1(R4), .in2(R8), .in3(R12), .in4(R16), .in5(R20), .in6(R24), .in7(R28),
    .out(multiplexer_3_out), .sel(ADDR[2:0]));
  Multiplexer #(.width(32), .enable("false")) multiplexer_4 (
    .in0(multiplexer_3_out), .in1(I0), .out(B0), .sel(not_1_out));
  Multiplexer #(.select(3), .width(32), .enable("false")) multiplexer_5 (
    .in0(R1), .in1(R5), .in2(R9), .in3(R13), .in4(R17), .in5(R21), .in6(R25), .in7(R29),
    .out(multiplexer_5_out), .sel(ADDR[2:0]));
  Multiplexer #(.width(32), .enable("false")) multiplexer_6 (
    .in0(multiplexer_5_out), .in1(I1), .out(B1), .sel(not_1_out));
  Multiplexer #(.select(3), .width(32), .enable("false")) multiplexer_7 (
    .in0(R2), .in1(R6), .in2(R10), .in3(R14), .in4(R18), .in5(R22), .in6(R26), .in7(R30),
    .out(multiplexer_7_out), .sel(ADDR[2:0]));
  Multiplexer #(.width(32), .enable("false")) multiplexer_8 (
    .in0(multiplexer_7_out), .in1(I2), .out(B2), .sel(not_1_out));
  Multiplexer #(.select(3), .width(32), .enable("false")) multiplexer_9 (
    .in0(R3), .in1(R7), .in2(R11), .in3(R15), .in4(R19), .in5(R23), .in6(R27), .in7(R31),
    .out(multiplexer_9_out), .sel(ADDR[2:0]));
  Multiplexer #(.width(32), .enable("false")) multiplexer_10 (
    .in0(multiplexer_9_out), .in1(I3), .out(B3), .sel(not_1_out));
  not not_1 (not_1_out, Hit);

  // Other names for the same wires on the sheet: LINE[2:0] = ADDR[2:0]; Tag[12:0] = ADDR[15:3]; RamR = RAM_READ;
  //   reset = CLR

  // Notes on the sheet:
  //   ADDR: pull=down
  //   Tag
  //   lineas
  //   Esta en Cache
  //   Valid
  //   Dirty
endmodule
